// Logisim project DE_Assignment1.circ as structural Verilog: 1 circuit, main circuit main
module main (
  input  W,
  input  X,
  input  Y,
  input  Z,
  output out_5,
  output out_6,
  output out_7,
  output out_8,
  output out_9,
  output out_10,
  output out_11
);

  wire A_out, A_prime_B_prime_C_out, A_prime_B_prime_C_prime_D_out, A_prime_B_prime_C_prime_out,
       A_prime_B_prime_D_out, and_1_out, B_out, B_prime_C_prime_D_out, BC_prime_D_prime_out, BC_prime_out,
       BCD_out, C_D_out, C_out, CD_out, D_out, not_1_out, not_2_out, not_3_out, not_4_out, not_5_out,
       not_6_out, not_7_out, not_8_out, not_9_out, not_10_out, not_11_out, not_12_out, not_13_out,
       not_14_out, not_15_out, W_prime_X_prime_Y_out, W_prime_XY_prime_Z_out, W_prime_YZ_out, WX_prime_Y_out,
       WY_prime_Z_prime_out, WZ_out, xnor_1_out, XY_prime_Z_prime_out, XYZ_prime_out;

  not not_1 (not_1_out, W);
  not not_2 (not_2_out, X);
  not not_3 (not_3_out, Y);
  not not_4 (not_4_out, Z);
  and WZ (WZ_out, W, Z);
  and WX_prime_Y (WX_prime_Y_out, W, not_2_out, Y);
  and XY_prime_Z_prime (XY_prime_Z_prime_out, X, not_3_out, not_4_out);
  and W_prime_YZ (W_prime_YZ_out, not_1_out, Y, Z);
  and WY_prime_Z_prime (WY_prime_Z_prime_out, W, not_3_out, not_4_out);
  and W_prime_X_prime_Y (W_prime_X_prime_Y_out, not_1_out, not_2_out, Y);
  and XYZ_prime (XYZ_prime_out, X, Y, not_4_out);
  and W_prime_XY_prime_Z (W_prime_XY_prime_Z_out, not_1_out, X, not_3_out, Z);
  or A (A_out, WZ_out, WX_prime_Y_out);
  or B (B_out, XY_prime_Z_prime_out, W_prime_YZ_out);
  or C (C_out, WY_prime_Z_prime_out, W_prime_X_prime_Y_out, XYZ_prime_out, W_prime_XY_prime_Z_out);
  and D (D_out, not_1_out, not_2_out, not_3_out);
  not not_5 (not_5_out, A_out);
  not not_6 (not_6_out, B_out);
  not not_7 (not_7_out, C_out);
  not not_8 (not_8_out, D_out);
  xnor xnor_1 (xnor_1_out, C_out, D_out);
  and BC_prime (BC_prime_out, B_out, not_7_out);
  and CD (CD_out, C_out, D_out);
  and A_prime_B_prime_D (A_prime_B_prime_D_out, not_5_out, not_6_out, D_out);
  and A_prime_B_prime_C (A_prime_B_prime_C_out, not_5_out, not_6_out, C_out);
  and A_prime_B_prime_C_prime (A_prime_B_prime_C_prime_out, not_5_out, not_6_out, not_7_out);
  and BCD (BCD_out, B_out, C_out, D_out);
  and A_prime_B_prime_C_prime_D (A_prime_B_prime_C_prime_D_out, not_5_out, not_6_out, not_7_out, D_out);
  and BC_prime_D_prime (BC_prime_D_prime_out, B_out, not_7_out, not_8_out);
  xor C_D (C_D_out, C_out, D_out);
  and and_1 (and_1_out, B_out, xnor_1_out);
  and B_prime_C_prime_D (B_prime_C_prime_D_out, not_6_out, not_7_out, D_out);
  or a_2 (out_5, A_prime_B_prime_C_prime_D_out, BC_prime_D_prime_out);
  and b_2 (out_6, B_out, C_D_out);
  and c_2 (out_7, not_6_out, C_out, not_8_out);
  or d_2 (out_8, and_1_out, B_prime_C_prime_D_out);
  or e (out_9, D_out, BC_prime_out);
  or f (out_10, CD_out, A_prime_B_prime_D_out, A_prime_B_prime_C_out);
  or g (out_11, A_prime_B_prime_C_prime_out, BCD_out);
  not not_9 (not_9_out, out_11);
  _7_Segment_Display u_7_segment_display_1 (
    .g(not_9_out), .f(not_13_out), .a(not_11_out), .b(not_12_out), .e(not_10_out), .d(not_15_out),
    .c(not_14_out));  // open: dp
  not not_10 (not_10_out, out_9);
  not not_11 (not_11_out, out_5);
  not not_12 (not_12_out, out_6);
  not not_13 (not_13_out, out_10);
  not not_14 (not_14_out, out_7);
  not not_15 (not_15_out, out_8);
endmodule
